// Logisim project 1-bit registor.circ as structural Verilog: 1 circuit, main circuit main
module main (
  input  Load,
  input  in_2,
  input  in_3,
  input  D1,
  output out_5
);

  wire and_1_out, and_2_out, not_1_out, or_1_out;

  not not_1 (not_1_out, Load);
  and and_1 (and_1_out, out_5, not_1_out);
  and and_2 (and_2_out, Load, D1);
  or or_1 (or_1_out, and_1_out, and_2_out);
  D_Flip_Flop #(.trigger("high")) d_ff_1 (.clk(in_2), .D(or_1_out), .Q(out_5), .en(in_3));  // open: Qn, preset, reset
endmodule
