// Logisim project 8-bit Computer.circ as structural Verilog
module _1_bit_Buffer_Register (
  input  in_1,
  input  in_2,
  input  in_3,
  input  in_4,
  output out_5
);

  wire and_1_out, and_2_out, not_1_out, or_1_out;

  not not_1 (not_1_out, in_2);
  and and_1 (and_1_out, in_2, in_3);
  or or_1 (or_1_out, and_1_out, and_2_out);
  and and_2 (and_2_out, not_1_out, out_5);
  D_Flip_Flop d_ff_1 (.clk(in_1), .D(or_1_out), .Q(out_5), .en(in_4));  // open: Qn, preset, reset
endmodule

module _8_bit_Buffer_Register (
  input  in_1,
  input  in_2,
  input  in_3,
  input  in_4,
  input  in_5,
  input  in_6,
  input  in_7,
  input  in_8,
  input  in_9,
  input  in_10,
  output out_11,
  output out_12,
  output out_13,
  output out_14,
  output out_15,
  output out_16,
  output out_17,
  output out_18
);

  wire clock_1_out;

  Clock clock_1 (.out(clock_1_out));
  _1_bit_Buffer_Register u_1_bit_buffer_register_1 (
    .in_2(in_1), .in_3(in_2), .in_4(in_10), .out_5(out_11), .in_1(clock_1_out));
  _1_bit_Buffer_Register u_1_bit_buffer_register_2 (
    .in_2(in_1), .in_3(in_3), .in_4(in_10), .out_5(out_12), .in_1(clock_1_out));
  _1_bit_Buffer_Register u_1_bit_buffer_register_3 (
    .in_2(in_1), .in_3(in_4), .in_4(in_10), .out_5(out_13), .in_1(clock_1_out));
  _1_bit_Buffer_Register u_1_bit_buffer_register_4 (
    .in_2(in_1), .in_3(in_5), .in_4(in_10), .out_5(out_14), .in_1(clock_1_out));
  _1_bit_Buffer_Register u_1_bit_buffer_register_5 (
    .in_2(in_1), .in_3(in_6), .in_4(in_10), .out_5(out_15), .in_1(clock_1_out));
  _1_bit_Buffer_Register u_1_bit_buffer_register_6 (
    .in_2(in_1), .in_3(in_7), .in_4(in_10), .out_5(out_16), .in_1(clock_1_out));
  _1_bit_Buffer_Register u_1_bit_buffer_register_7 (
    .in_2(in_1), .in_3(in_8), .in_4(in_10), .out_5(out_17), .in_1(clock_1_out));
  _1_bit_Buffer_Register u_1_bit_buffer_register_8 (
    .in_2(in_1), .in_3(in_9), .in_4(in_10), .out_5(out_18), .in_1(clock_1_out));
endmodule
